# Fritzing sketch Schaltplan (saved by Fritzing 0.9.2b)
circuit board: 6.88566cm x 5.36311cm
breadboards: 2

parts:
  LCD1 = LCD screen
  R2 = Resistor [tolerance=±5% resistance=220 package=THT]
  Contrast1 = Rotary Potentiometer (Small) [maximum_resistance=100kΩ package=THT]
  Arduino1 = Arduino Uno (Rev3)
  U1 = mini DIN 6 Connector [package=mini-din6]  # not connected
  LED1 = DUO LED RG [package="5 mm [THT]"]
  Power_plug1 = Power plug

nets (from the breadboard view):
  GND: LCD1.VSS, LCD1.R/W, LCD1.LED-, Contrast1.leg1, Arduino1.GND, LED1.red_anode, Power_plug1.GND
  VDD: LCD1.VDD, R2.Pin_1, Contrast1.leg2, LED1.green_anode, Power_plug1.VCC
  N1: LCD1.V0, Contrast1.wiper
  N2: LCD1.RS, Arduino1.D12/MISO
  N3: LCD1.E, Arduino1.D11_PWM/MOSI
  N4: LCD1.DB4, Arduino1.D6_PWM
  N5: LCD1.DB5, Arduino1.D5_PWM
  N6: LCD1.DB6, Arduino1.D4
  N7: LCD1.DB7, Arduino1.D3_PWM
  N8: LCD1.LED+, R2.Pin_0
  N9: Arduino1.D10_PWM/SS, LED1.common_cathode

notes:
  Code and more on character LCDs at http://arduino.cc/en/Tutorial/LiquidCrystal
